// Logisim project Roma.circ as structural Verilog
module _1_2_somador (
  input  A0,
  input  B0,
  output soma,
  output co
);

  and and_1 (co, B0, A0);
  xor xor_1 (soma, A0, B0);
endmodule

module somador_comp (
  input  Ci0,
  input  A0,
  input  B0,
  output S0,
  output Co0
);

  wire n1_2_somador_1_co, n1_2_somador_1_soma, n1_2_somador_2_co;

  _1_2_somador u_1_2_somador_1 (.A0(A0), .B0(B0), .co(n1_2_somador_1_co), .soma(n1_2_somador_1_soma));
  or or_1 (Co0, n1_2_somador_1_co, n1_2_somador_2_co);
  _1_2_somador u_1_2_somador_2 (.A0(Ci0), .B0(n1_2_somador_1_soma), .co(n1_2_somador_2_co), .soma(S0));
endmodule

module somador_4_bits (
  input  ci0,
  input  a0,
  input  b0,
  input  a1,
  input  b1,
  input  a2,
  input  b2,
  input  a3,
  input  b3,
  output S0,
  output S1,
  output S2,
  output S3,
  output C3
);

  wire somador_comp_1_co0, somador_comp_2_co0, somador_comp_3_co0;

  somador_comp somador_comp_1 (.Ci0(ci0), .A0(a0), .B0(b0), .Co0(somador_comp_1_co0), .S0(S0));
  somador_comp somador_comp_2 (.Ci0(somador_comp_1_co0), .A0(a1), .B0(b1), .Co0(somador_comp_2_co0), .S0(S1));
  somador_comp somador_comp_3 (.Ci0(somador_comp_2_co0), .A0(a2), .B0(b2), .Co0(somador_comp_3_co0), .S0(S2));
  somador_comp somador_comp_4 (.Ci0(somador_comp_3_co0), .A0(a3), .B0(b3), .Co0(C3), .S0(S3));
endmodule

module somador (
  input  A0,
  input  A1,
  input  A2,
  input  cin,
  input  A3,
  input  B0,
  input  B1,
  input  B2,
  input  B3,
  output overflow,
  output cout,
  output S0,
  output S1,
  output S2,
  output S3
);

  wire decodificador_1_a, decodificador_1_b, decodificador_1_c, decodificador_1_d, decodificador_1_e,
       decodificador_1_f, decodificador_1_g, decodificador_2_a, decodificador_2_b, decodificador_2_c,
       decodificador_2_d, decodificador_2_e, decodificador_2_f, decodificador_2_g, decodificador_3_a,
       decodificador_3_b, decodificador_3_c, decodificador_3_d, decodificador_3_e, decodificador_3_f,
       decodificador_3_g;

  somador_com_overflow somador_com_overflow_1 (
    .a0(B0), .b0(A0), .a1(B1), .b1(A1), .a2(B2), .b2(A2), .a3(B3), .b3(A3), .ci0(cin), .C3(cout), .S0(S0),
    .S1(S1), .S2(S2), .S3(S3), .Overflow(overflow));
  decodificador decodificador_1 (
    .e3(A3), .e2(A2), .e1(A1), .e0(A0), .a(decodificador_1_a), .b(decodificador_1_b), .c(decodificador_1_c),
    .d(decodificador_1_d), .e(decodificador_1_e), .f(decodificador_1_f), .g(decodificador_1_g));
  decodificador decodificador_2 (
    .e3(B3), .e2(B2), .e1(B1), .e0(B0), .a(decodificador_2_a), .b(decodificador_2_b), .c(decodificador_2_c),
    .d(decodificador_2_d), .e(decodificador_2_e), .f(decodificador_2_f), .g(decodificador_2_g));
  _7_Segment_Display u_7_segment_display_1 (
    .g(decodificador_1_g), .f(decodificador_1_f), .a(decodificador_1_a), .b(decodificador_1_b),
    .e(decodificador_1_e), .d(decodificador_1_d), .c(decodificador_1_c));  // open: dp
  _7_Segment_Display u_7_segment_display_2 (
    .g(decodificador_2_g), .f(decodificador_2_f), .a(decodificador_2_a), .b(decodificador_2_b),
    .e(decodificador_2_e), .d(decodificador_2_d), .c(decodificador_2_c));  // open: dp
  decodificador decodificador_3 (
    .e3(S3), .e2(S2), .e1(S1), .e0(S0), .a(decodificador_3_a), .b(decodificador_3_b), .c(decodificador_3_c),
    .d(decodificador_3_d), .e(decodificador_3_e), .f(decodificador_3_f), .g(decodificador_3_g));
  _7_Segment_Display u_7_segment_display_3 (
    .g(decodificador_3_g), .f(decodificador_3_f), .a(decodificador_3_a), .b(decodificador_3_b),
    .e(decodificador_3_e), .d(decodificador_3_d), .c(decodificador_3_c));  // open: dp
endmodule

module decodificador (
  input  e3,
  input  e2,
  input  e1,
  input  e0,
  output a,
  output b,
  output c,
  output d,
  output e,
  output f,
  output g
);

  wire and_1_out, and_2_out, and_3_out, and_4_out, and_5_out, and_6_out, and_7_out, and_8_out, and_9_out,
       and_10_out, and_11_out, and_12_out, and_13_out, and_14_out, and_15_out, and_16_out, and_17_out,
       and_18_out, and_19_out, and_20_out, and_21_out, and_22_out, and_23_out, and_24_out, and_25_out,
       and_26_out, and_27_out, and_28_out, and_29_out, and_30_out, and_31_out, and_32_out, and_33_out,
       and_34_out, and_35_out, and_36_out, not_1_out, not_2_out, not_3_out, not_4_out, not_5_out, not_6_out,
       not_7_out, not_8_out, not_9_out, not_10_out, not_11_out, not_12_out, not_13_out, not_14_out,
       not_15_out, not_16_out, not_17_out, not_18_out, not_19_out, not_20_out, not_21_out, not_22_out,
       not_23_out, not_24_out, not_25_out, not_26_out, not_27_out, not_28_out, not_29_out, not_30_out,
       not_31_out, not_32_out, not_33_out, not_34_out, not_35_out, not_36_out, not_37_out, not_38_out,
       not_39_out, not_40_out, not_41_out, not_42_out, not_43_out, not_44_out;

  not not_1 (not_1_out, e2);
  and and_1 (and_1_out, not_1_out, not_2_out);
  not not_2 (not_2_out, e0);
  not not_3 (not_3_out, e3);
  and and_2 (and_2_out, not_3_out, e1);
  not not_4 (not_4_out, e3);
  and and_3 (and_3_out, not_4_out, e2, e0);
  and and_4 (and_4_out, e2, e1);
  and and_5 (and_5_out, e3, not_5_out, not_6_out);
  not not_5 (not_5_out, e2);
  not not_6 (not_6_out, e1);
  and and_6 (and_6_out, e3, not_7_out);
  not not_7 (not_7_out, e0);
  not not_8 (not_8_out, e3);
  and and_7 (and_7_out, not_8_out, not_9_out);
  not not_9 (not_9_out, e2);
  not not_10 (not_10_out, e3);
  not not_11 (not_11_out, e1);
  and and_8 (and_8_out, not_10_out, not_11_out, not_12_out);
  not not_12 (not_12_out, e0);
  not not_13 (not_13_out, e2);
  and and_9 (and_9_out, not_13_out, not_14_out);
  not not_14 (not_14_out, e0);
  not not_15 (not_15_out, e3);
  and and_10 (and_10_out, not_15_out, e1, e0);
  not not_16 (not_16_out, e1);
  and and_11 (and_11_out, e3, not_16_out, e0);
  not not_17 (not_17_out, e3);
  and and_12 (and_12_out, not_17_out, not_18_out);
  not not_18 (not_18_out, e1);
  not not_19 (not_19_out, e3);
  and and_13 (and_13_out, not_19_out, e0);
  not not_20 (not_20_out, e1);
  and and_14 (and_14_out, not_20_out, e0);
  not not_21 (not_21_out, e3);
  and and_15 (and_15_out, not_21_out, e2);
  and and_16 (and_16_out, e3, not_22_out);
  not not_22 (not_22_out, e2);
  not not_23 (not_23_out, e3);
  and and_17 (and_17_out, not_23_out, not_24_out, not_25_out);
  not not_24 (not_24_out, e2);
  not not_25 (not_25_out, e0);
  not not_26 (not_26_out, e3);
  and and_18 (and_18_out, not_26_out, e1);
  not not_27 (not_27_out, e3);
  and and_19 (and_19_out, not_27_out, e2, e0);
  and and_20 (and_20_out, e3, not_28_out);
  not not_28 (not_28_out, e1);
  and and_21 (and_21_out, e3, not_29_out, e0);
  not not_29 (not_29_out, e2);
  and and_22 (and_22_out, e3, e2, not_30_out);
  not not_30 (not_30_out, e0);
  not not_31 (not_31_out, e2);
  and and_23 (and_23_out, not_31_out, not_32_out);
  not not_32 (not_32_out, e0);
  and and_24 (and_24_out, e1, not_33_out);
  not not_33 (not_33_out, e0);
  and and_25 (and_25_out, e3, e1);
  and and_26 (and_26_out, e3, e2);
  not not_34 (not_34_out, e1);
  and and_27 (and_27_out, not_34_out, not_35_out);
  not not_35 (not_35_out, e0);
  not not_36 (not_36_out, e3);
  and and_28 (and_28_out, not_36_out, e2, not_37_out);
  not not_37 (not_37_out, e1);
  and and_29 (and_29_out, e2, not_38_out);
  not not_38 (not_38_out, e0);
  and and_30 (and_30_out, e3, not_39_out);
  not not_39 (not_39_out, e2);
  and and_31 (and_31_out, e3, e1);
  not not_40 (not_40_out, e2);
  and and_32 (and_32_out, not_40_out, e1);
  and and_33 (and_33_out, e1, not_41_out);
  not not_41 (not_41_out, e0);
  not not_42 (not_42_out, e3);
  and and_34 (and_34_out, not_42_out, e2, not_43_out);
  not not_43 (not_43_out, e1);
  and and_35 (and_35_out, e3, not_44_out);
  not not_44 (not_44_out, e2);
  and and_36 (and_36_out, e3, e0);
  or or_1 (b, and_7_out, and_8_out, and_9_out, and_10_out, and_11_out);
  or or_2 (c, and_12_out, and_13_out, and_14_out, and_15_out, and_16_out);
  or or_3 (e, and_23_out, and_24_out, and_25_out, and_26_out);
  or or_4 (f, and_27_out, and_28_out, and_29_out, and_30_out, and_31_out);
  or or_5 (g, and_32_out, and_33_out, and_34_out, and_35_out, and_36_out);
  or or_6 (a, and_1_out, and_2_out, and_3_out, and_4_out, and_5_out, and_6_out);
  or or_7 (d, and_17_out, and_18_out, and_19_out, and_20_out, and_21_out, and_22_out);
endmodule

module somador_com_overflow (
  input  ci0,
  input  a0,
  input  b0,
  input  a1,
  input  b1,
  input  a2,
  input  b2,
  input  a3,
  input  b3,
  output S0,
  output S1,
  output S2,
  output S3,
  output Overflow,
  output C3
);

  wire somador_comp_1_co0, somador_comp_2_co0, somador_comp_3_co0;

  somador_comp somador_comp_1 (.Ci0(ci0), .A0(a0), .B0(b0), .Co0(somador_comp_1_co0), .S0(S0));
  somador_comp somador_comp_2 (.Ci0(somador_comp_1_co0), .A0(a1), .B0(b1), .Co0(somador_comp_2_co0), .S0(S1));
  somador_comp somador_comp_3 (.Ci0(somador_comp_2_co0), .A0(a2), .B0(b2), .Co0(somador_comp_3_co0), .S0(S2));
  somador_comp somador_comp_4 (.Ci0(somador_comp_3_co0), .A0(a3), .B0(b3), .Co0(C3), .S0(S3));
  xor xor_1 (Overflow, somador_comp_3_co0, C3);
endmodule
